# Fritzing sketch Sketch (saved by Fritzing 0.9.3b)
breadboards: 1

parts:
  Part1 = Arduino Uno (Rev3) - ICSP
  R1 = Resistor [tolerance=±5% resistance=10k package="0603 [SMD]"]
  R2 = Resistor [tolerance=±5% resistance=10k package="0603 [SMD]"]
  R3 = Resistor [tolerance=±5% resistance=10k package="0603 [SMD]"]
  S1 = Pushbutton [package="[SMD]"]
  S2 = Pushbutton [package="[SMD]"]
  S3 = Pushbutton [package="[SMD]"]
  DS1 = DS18B20 1-Wire Temperature Sensor [part_number=DS18B20]
  R4 = Resistor [tolerance=±5% resistance=4.7k package="0603 [SMD]"]
  DS2 = DS18B20 1-Wire Temperature Sensor [part_number=DS18B20]
  DS3 = DS18B20 1-Wire Temperature Sensor [part_number=DS18B20]
  J1 = Piezo Speaker
  DS4 = DS18B20 1-Wire Temperature Sensor [part_number=DS18B20]
  Part2 = OLED Monochrome 128x64 0.96 inch [part_number=326]

nets:
  N1: Part1.ICSP_MOSI, Part1.D11_PWM/MOSI, Part2.DC_SA0
  N2: Part1.D8, R1.Pin_0, S1.Pin_3, S1.Pin_4
  N3: Part1.D9_PWM, Part2.MOSI_SDA
  N4: Part1.D10_PWM/SS, Part2.SCLK_SCK
  N5: Part1.D12/MISO, Part2.CS
  N6: Part1.D13/SCK, Part2.RESET
  GND: Part1.GND, R1.Pin_1, R2.Pin_1, R3.Pin_1, DS1.GND, DS2.GND, DS3.GND, J1.pin1, DS4.GND, Part2.GND
  N7: Part1.D2, DS1.DQ, R4.Pin_1, DS2.DQ, DS3.DQ, DS4.DQ
  N8: Part1.D4, R2.Pin_0, S3.Pin_3, S3.Pin_4
  N9: Part1.D6_PWM, R3.Pin_0, S2.Pin_3, S2.Pin_4
  N10: Part1.D7, J1.pin2
  VDD: Part1.5V, S1.Pin_1, S1.Pin_2, S2.Pin_1, S2.Pin_2, S3.Pin_1, S3.Pin_2, DS1.VDD, DS2.VDD, DS3.VDD, DS4.VDD, Part2.VIN

notes:
  FAN PWM
  PUMP PWM

custom parts:
  OLED Monochrome 128x64 0.96 inch: These displays are small, only about 1" diameter, but very readable due to the high contrast of an OLED display. This display is made of 128x64 individual white OLED pixels, each one is turned on or off by the controller chip. Because the display makes its own light, no backlight is required. This reduces the power required to run the OLED and is why the display has such high contrast; we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
